// Logisim project Intento1Tarea2.circ as structural Verilog: 1 circuit, main circuit main
module main (
  input  T,
  input  w_A,
  input  x_A,
  input  y_A,
  input  z_A,
  input  w_B,
  input  x_B,
  input  y_B,
  input  z_B,
  input  in_10,
  input  in_11,
  input  in_12,
  input  in_13,
  input  in_14,
  input  in_15,
  input  in_16,
  input  in_17,
  input  in_18,
  output o_0,
  output o_1,
  output o_2,
  output o_3,
  output out_23,
  output out_24,
  output out_25,
  output out_26
);

  wire and_1_out, and_2_out, and_3_out, nor_1_out, nor_2_out, nor_3_out, nor_4_out, nor_5_out, nor_6_out,
       nor_7_out, nor_8_out, nor_9_out, nor_10_out, nor_11_out, nor_12_out, nor_13_out, or_5_out, or_6_out,
       or_7_out, xor_3_out;

  nor nor_1 (nor_1_out, T, T);
  and and_1 (and_1_out, in_12, in_13, in_14);
  nor nor_2 (nor_2_out, in_12, in_13);
  nor nor_3 (nor_3_out, in_13, in_14);
  nor nor_4 (nor_4_out, in_12, in_14);
  and and_2 (and_2_out, in_16, in_17, in_18);
  nor nor_5 (nor_5_out, in_16, in_17);
  nor nor_6 (nor_6_out, in_17, in_18);
  nor nor_7 (nor_7_out, in_16, in_18);
  or or_1 (o_0, w_A, w_B);
  or or_2 (o_1, x_A, x_B);
  or or_3 (o_2, y_A, y_B);
  or or_4 (o_3, z_A, z_B);
  or or_5 (or_5_out, and_1_out, nor_2_out, nor_3_out, nor_4_out);
  nor nor_8 (nor_8_out, in_12, in_13, in_14);
  or or_6 (or_6_out, and_2_out, nor_5_out, nor_6_out, nor_7_out);
  nor nor_9 (nor_9_out, in_16, in_17, in_18);
  xor xor_1 (out_23, or_5_out, nor_8_out);
  xor xor_2 (out_25, or_6_out, nor_9_out);
  // AND_Gate and_3 has open pins: out=and_3_out
  // NOR_Gate nor_10 has open pins: out=nor_10_out
  // NOR_Gate nor_11 has open pins: out=nor_11_out
  // NOR_Gate nor_12 has open pins: out=nor_12_out
  or or_7 (or_7_out, and_3_out, nor_10_out, nor_11_out, nor_12_out);
  // NOR_Gate nor_13 has open pins: out=nor_13_out
  xor xor_3 (xor_3_out, or_7_out, nor_13_out);

  // Notes on the sheet:
  //   Solo pasa True se T es 0
  //   A+B
  //   g(w,x,y,z)
  //   f(x,y,z)
  //   f(x,y,z)
endmodule
