// Logisim project Intento2Tarea2.circ as structural Verilog
module Inento2Tarea2 (
  input  T,
  input  wA,
  input  xA,
  input  yA,
  input  zA,
  input  wB,
  input  xB,
  input  yB,
  input  zB,
  output o0,
  output o1,
  output o2,
  output o3
);

  wire and_1_out, and_2_out, not_1_out, not_2_out;

  not not_1 (not_1_out, xA);
  not not_2 (not_2_out, yA);
  and and_1 (and_1_out, xA, yA, zA);
  and and_2 (and_2_out, not_1_out, not_2_out);
  or or_1 (o0, and_1_out, and_2_out);
endmodule

module Intento2Tarea2 (
  input  T,
  input  [3:0] A,
  input  [3:0] B,
  output [3:0] O
);

  wire and_1_out, and_2_out, and_3_out, and_4_out, and_5_out, and_6_out, and_7_out, and_8_out, and_9_out,
       and_10_out, and_11_out, and_12_out, and_13_out, and_14_out, and_15_out, and_16_out, and_17_out,
       and_18_out, and_19_out, and_20_out, and_21_out, and_22_out, and_23_out, and_24_out, and_25_out,
       and_26_out, and_27_out, and_28_out, and_29_out, and_30_out, and_31_out, and_32_out, not_1_out,
       not_2_out, not_3_out, not_4_out, not_5_out, not_6_out, not_7_out, not_8_out, not_9_out;

  not not_1 (not_1_out, T);
  not not_2 (not_2_out, A[3]);
  not not_3 (not_3_out, A[2]);
  not not_4 (not_4_out, A[1]);
  not not_5 (not_5_out, A[0]);
  not not_6 (not_6_out, B[3]);
  not not_7 (not_7_out, B[2]);
  not not_8 (not_8_out, B[1]);
  not not_9 (not_9_out, B[0]);
  and and_1 (and_1_out, not_1_out, B[3]);
  and and_2 (and_2_out, not_1_out, A[3]);
  and and_3 (and_3_out, T, not_3_out, not_4_out, A[0]);
  and and_4 (and_4_out, T, not_3_out, A[1], not_5_out);
  and and_5 (and_5_out, T, A[2], not_4_out, not_5_out);
  and and_6 (and_6_out, T, A[2], A[1], A[0]);
  and and_7 (and_7_out, not_1_out, B[2]);
  and and_8 (and_8_out, not_1_out, A[2]);
  and and_9 (and_9_out, not_2_out, A[2], not_4_out, not_5_out);
  and and_10 (and_10_out, not_2_out, A[2], A[1], A[0]);
  and and_11 (and_11_out, A[3], A[2], not_4_out, A[0]);
  and and_12 (and_12_out, A[3], A[2], A[1], not_5_out);
  and and_13 (and_13_out, T, not_2_out, not_3_out, not_4_out, A[0]);
  and and_14 (and_14_out, T, not_2_out, not_3_out, A[1], not_5_out);
  and and_15 (and_15_out, T, A[3], not_3_out, not_4_out, not_5_out);
  and and_16 (and_16_out, T, A[3], not_3_out, A[1], A[0]);
  and and_17 (and_17_out, not_1_out, A[3]);
  and and_18 (and_18_out, not_1_out, B[3]);
  and and_19 (and_19_out, T, not_7_out, not_8_out, B[0]);
  and and_20 (and_20_out, T, not_7_out, B[1], not_9_out);
  and and_21 (and_21_out, T, B[2], not_8_out, not_9_out);
  and and_22 (and_22_out, T, B[2], B[1], B[0]);
  and and_23 (and_23_out, not_1_out, B[0]);
  and and_24 (and_24_out, not_6_out, not_7_out, not_8_out, B[0]);
  and and_25 (and_25_out, not_6_out, B[2], B[1], B[0]);
  and and_26 (and_26_out, B[3], not_7_out, B[1], B[0]);
  and and_27 (and_27_out, B[3], B[2], not_8_out, B[0]);
  and and_28 (and_28_out, not_1_out, A[0]);
  and and_29 (and_29_out, T, not_6_out, not_7_out, B[1], not_9_out);
  and and_30 (and_30_out, T, not_6_out, B[2], not_8_out, not_9_out);
  and and_31 (and_31_out, T, B[3], not_7_out, not_8_out, not_9_out);
  and and_32 (and_32_out, T, B[3], B[2], B[1], not_9_out);
  or or_1 (O[3], and_1_out, and_2_out, and_3_out, and_4_out, and_5_out, and_6_out);
  or or_2 (O[2], and_7_out, and_8_out, and_9_out, and_10_out, and_11_out, and_12_out, and_13_out, and_14_out, and_15_out, and_16_out);
  or or_3 (O[1], and_17_out, and_18_out, and_19_out, and_20_out, and_21_out, and_22_out);
  or or_4 (O[0], and_23_out, and_24_out, and_25_out, and_26_out, and_27_out, and_28_out, and_29_out, and_30_out, and_31_out, and_32_out);
endmodule
