// Logisim project fx.circ as structural Verilog
module try (
  input  in_1,
  input  in_2,
  input  in_3
);
endmodule

module f (
  input  x,
  input  y,
  input  z,
  output o
);

  wire and_1_out, and_2_out, and_3_out, and_4_out, not_1_out, not_2_out, not_3_out;

  not not_1 (not_1_out, x);
  not not_2 (not_2_out, y);
  not not_3 (not_3_out, z);
  and and_1 (and_1_out, not_1_out, not_2_out, z);
  and and_2 (and_2_out, not_1_out, y, not_3_out);
  and and_3 (and_3_out, x, not_2_out, not_3_out);
  and and_4 (and_4_out, x, y, z);
  or or_1 (o, and_1_out, and_2_out, and_3_out, and_4_out);
endmodule
