// Logisim project intento3.circ as structural Verilog: 2 circuits, main circuit main
module main (
  input  t,
  input  wA,
  input  x_A,
  input  y_A,
  input  z_A,
  input  wB,
  input  x_B,
  input  y_B,
  input  z_B
);

  wire and_1_out, and_2_out, and_3_out, and_4_out, circled_1_a, circled_1_b, circled_1_c, circled_1_d,
       circled_1_e, circled_1_f, circled_1_g, multiplexer_1_out, multiplexer_2_out, multiplexer_3_out,
       multiplexer_4_out, multiplexer_5_out, multiplexer_6_out, not_1_out, not_2_out, or_1_out, or_2_out,
       Resto_out, Suma_out, xor_1_out, xor_2_out, xor_3_out, xor_4_out, xor_5_out, xor_6_out, xor_7_out,
       xor_8_out, xor_9_out, xor_10_out;

  and Resto (Resto_out, z_A, z_B);
  xor Suma (Suma_out, z_A, z_B);
  and and_1 (and_1_out, y_B, y_A);
  xor xor_1 (xor_1_out, y_A, y_B);
  and and_2 (and_2_out, x_A, x_B);
  xor xor_2 (xor_2_out, x_A, x_B);
  and and_3 (and_3_out, xor_1_out, Resto_out);
  xor xor_3 (xor_3_out, x_A, y_A);
  xor xor_4 (xor_4_out, wA, wB);
  xor xor_5 (xor_5_out, x_B, y_B);
  and and_4 (and_4_out, xor_2_out, or_1_out);
  or or_1 (or_1_out, and_3_out, and_1_out);
  xor xor_6 (xor_6_out, xor_3_out, z_A);
  xor xor_7 (xor_7_out, xor_5_out, z_B);
  xor xor_8 (xor_8_out, xor_2_out, or_1_out);
  xor xor_9 (xor_9_out, xor_1_out, Resto_out);
  or or_2 (or_2_out, and_4_out, and_2_out);
  Multiplexer #(.enable("false")) multiplexer_1 (.in0(xor_6_out), .in1(not_1_out), .out(multiplexer_1_out), .sel(wA));
  not not_1 (not_1_out, xor_6_out);
  xor xor_10 (xor_10_out, xor_4_out, or_2_out);
  not not_2 (not_2_out, xor_7_out);
  Multiplexer #(.enable("false")) multiplexer_2 (.in0(xor_7_out), .in1(not_2_out), .out(multiplexer_2_out), .sel(wB));
  Multiplexer #(.enable("false")) multiplexer_3 (.in0(xor_10_out), .in1(xor_6_out), .out(multiplexer_3_out), .sel(t));
  Multiplexer #(.enable("false")) multiplexer_4 (
    .in0(xor_8_out), .in1(multiplexer_1_out), .out(multiplexer_4_out), .sel(t));
  Multiplexer #(.enable("false")) multiplexer_5 (.in0(xor_9_out), .in1(xor_7_out), .out(multiplexer_5_out), .sel(t));
  Multiplexer #(.enable("false")) multiplexer_6 (
    .in0(Suma_out), .in1(multiplexer_2_out), .out(multiplexer_6_out), .sel(t));
  circLed circled_1 (
    .o0(multiplexer_3_out), .o1(multiplexer_4_out), .o2(multiplexer_5_out), .o3(multiplexer_6_out),
    .a(circled_1_a), .b(circled_1_b), .c(circled_1_c), .d(circled_1_d), .e(circled_1_e), .f(circled_1_f),
    .g(circled_1_g));
  LED led_1 (.in(circled_1_a));
  LED led_2 (.in(circled_1_a));
  LED led_3 (.in(circled_1_f));
  LED led_4 (.in(circled_1_f));
  LED led_5 (.in(circled_1_f));
  LED led_6 (.in(circled_1_g));
  LED led_7 (.in(circled_1_g));
  LED led_8 (.in(circled_1_e));
  LED led_9 (.in(circled_1_e));
  LED led_10 (.in(circled_1_e));
  LED led_11 (.in(circled_1_d));
  LED led_12 (.in(circled_1_d));
  LED led_13 (.in(circled_1_a));
  LED led_14 (.in(circled_1_b));
  LED led_15 (.in(circled_1_b));
  LED led_16 (.in(circled_1_b));
  LED led_17 (.in(circled_1_g));
  LED led_18 (.in(circled_1_c));
  LED led_19 (.in(circled_1_c));
  LED led_20 (.in(circled_1_c));
  LED led_21 (.in(circled_1_d));

  // Notes on the sheet:
  //   f(xA, yA, zA)
  //   f(xB, yB, zB)
  //   A+B
  //   g(wA, xA, yA, zA)
  //   g(wB, xB, yB, zB)
  //   T
  //   Bin to Hex
endmodule

module circLed (
  input  o0,
  input  o1,
  input  o2,
  input  o3,
  output a,
  output b,
  output c,
  output d,
  output e,
  output f,
  output g
);

  wire and_1_out, and_2_out, and_3_out, and_4_out, and_5_out, and_6_out, and_7_out, and_8_out, and_9_out,
       and_10_out, and_11_out, and_12_out, and_13_out, and_14_out, and_15_out, and_16_out, and_17_out,
       and_18_out, and_19_out, and_20_out, and_21_out, and_22_out, and_23_out, and_24_out, and_25_out,
       and_26_out, and_27_out, and_28_out, and_29_out, and_30_out, and_31_out, and_32_out, and_33_out,
       and_34_out, and_35_out, not_1_out, not_2_out, not_3_out, not_4_out;

  not not_1 (not_1_out, o0);
  not not_2 (not_2_out, o1);
  not not_3 (not_3_out, o2);
  not not_4 (not_4_out, o3);
  and and_1 (and_1_out, not_2_out, not_4_out);
  and and_2 (and_2_out, not_1_out, o2);
  and and_3 (and_3_out, not_1_out, o1, o3);
  and and_4 (and_4_out, o1, o2);
  and and_5 (and_5_out, o0, not_2_out, not_3_out);
  and and_6 (and_6_out, o0, not_4_out);
  and and_7 (and_7_out, not_1_out, not_2_out);
  and and_8 (and_8_out, not_1_out, not_3_out, not_4_out);
  and and_9 (and_9_out, not_2_out, not_4_out);
  and and_10 (and_10_out, not_1_out, o2, o3);
  and and_11 (and_11_out, o0, not_3_out, o3);
  and and_12 (and_12_out, not_1_out, not_3_out);
  and and_13 (and_13_out, not_1_out, o3);
  and and_14 (and_14_out, not_3_out, o3);
  and and_15 (and_15_out, not_1_out, o1);
  and and_16 (and_16_out, o0, not_2_out);
  and and_17 (and_17_out, not_1_out, not_2_out, not_4_out);
  and and_18 (and_18_out, not_2_out, o2, o3);
  and and_19 (and_19_out, o1, not_3_out, o3);
  and and_20 (and_20_out, o1, o2, not_4_out);
  and and_21 (and_21_out, o0, not_3_out);
  and and_22 (and_22_out, not_2_out, not_4_out);
  and and_23 (and_23_out, o2, not_4_out);
  and and_24 (and_24_out, o0, o2);
  and and_25 (and_25_out, o0, o1);
  and and_26 (and_26_out, not_3_out, not_4_out);
  and and_27 (and_27_out, not_1_out, o1, not_3_out);
  and and_28 (and_28_out, o1, not_4_out);
  and and_29 (and_29_out, o0, not_2_out);
  and and_30 (and_30_out, o0, o2);
  and and_31 (and_31_out, not_2_out, o2);
  and and_32 (and_32_out, o2, not_4_out);
  and and_33 (and_33_out, not_1_out, o1, not_3_out);
  and and_34 (and_34_out, o0, not_2_out);
  and and_35 (and_35_out, o0, o3);
  or or_1 (a, and_1_out, and_2_out, and_3_out, and_4_out, and_5_out, and_6_out);
  or or_2 (b, and_7_out, and_8_out, and_9_out, and_10_out, and_11_out);
  or or_3 (c, and_12_out, and_13_out, and_14_out, and_15_out, and_16_out);
  or or_4 (d, and_17_out, and_18_out, and_19_out, and_20_out, and_21_out);
  or or_5 (e, and_22_out, and_23_out, and_24_out, and_25_out);
  or or_6 (f, and_26_out, and_27_out, and_28_out, and_29_out, and_30_out);
  or or_7 (g, and_31_out, and_32_out, and_33_out, and_34_out, and_35_out);
endmodule
