// Logisim project ledofc.circ as structural Verilog: 10 circuits, main circuit main
module main (
  input  [6:0] in_1,
  input  [6:0] in_2,
  input  [6:0] in_3,
  input  [6:0] in_4,
  input  [6:0] in_5,
  input  [6:0] in_6,
  input  [6:0] in_7,
  input  [6:0] in_8,
  input  [6:0] in_9,
  input  [6:0] in_10,
  input  [6:0] in_11,
  input  [6:0] in_12,
  input  [3:0] in_13
);

  wire undriven, undriven_2, undriven_3, undriven_4, undriven_5, undriven_6, undriven_7;
  wire [6:0] multiplexer_1_out;

  Multiplexer #(.enable("false"), .select(4), .width(7)) multiplexer_1 (
    .in0(7'b1111110), .in1(7'b0110000), .in2(7'b1101101), .in3(7'b1111001), .in4(in_1), .in5(in_2),
    .in6(in_3), .in7(in_4), .in8(in_5), .in9(in_6), .in10(in_7), .in11(in_8), .in12(in_9), .in13(in_10),
    .in14(in_11), .in15(in_12), .out(multiplexer_1_out), .sel(in_13));
  LED led_1 (.in(multiplexer_1_out[6]));
  LED led_2 (.in(multiplexer_1_out[6]));
  LED led_3 (.in(multiplexer_1_out[1]));
  LED led_4 (.in(multiplexer_1_out[1]));
  LED led_5 (.in(multiplexer_1_out[1]));
  LED led_6 (.in(multiplexer_1_out[0]));
  LED led_7 (.in(multiplexer_1_out[0]));
  LED led_8 (.in(multiplexer_1_out[2]));
  LED led_9 (.in(multiplexer_1_out[2]));
  LED led_10 (.in(multiplexer_1_out[2]));
  LED led_11 (.in(multiplexer_1_out[3]));
  LED led_12 (.in(multiplexer_1_out[3]));
  LED led_13 (.in(undriven_3));
  LED led_14 (.in(undriven_3));
  LED led_15 (.in(undriven));
  LED led_16 (.in(undriven));
  LED led_17 (.in(undriven));
  LED led_18 (.in(undriven_4));
  LED led_19 (.in(undriven_4));
  LED led_20 (.in(undriven_2));
  LED led_21 (.in(undriven_2));
  LED led_22 (.in(undriven_2));
  LED led_23 (.in(undriven_5));
  LED led_24 (.in(undriven_5));
  LED led_25 (.in(multiplexer_1_out[6]));
  LED led_26 (.in(multiplexer_1_out[5]));
  LED led_27 (.in(multiplexer_1_out[5]));
  LED led_28 (.in(multiplexer_1_out[5]));
  LED led_29 (.in(multiplexer_1_out[0]));
  LED led_30 (.in(multiplexer_1_out[4]));
  LED led_31 (.in(multiplexer_1_out[4]));
  LED led_32 (.in(multiplexer_1_out[4]));
  LED led_33 (.in(multiplexer_1_out[3]));
  LED led_34 (.in(undriven_3));
  LED led_35 (.in(undriven_6));
  LED led_36 (.in(undriven_6));
  LED led_37 (.in(undriven_6));
  LED led_38 (.in(undriven_4));
  LED led_39 (.in(undriven_7));
  LED led_40 (.in(undriven_7));
  LED led_41 (.in(undriven_7));
  LED led_42 (.in(undriven_5));

  // Notes on the sheet:
  //   f
  //   e
  //   a
  //   g
  //   d
  //   b
  //   c
endmodule

module fx (
  input  x,
  input  y,
  input  z,
  output f
);

  wire xor_1_out;

  xor xor_1 (xor_1_out, x, y);
  xor xor_2 (f, xor_1_out, z);
endmodule

module sumac1 (
  input  yA1,
  input  yB1,
  input  c,
  output O2
);

  wire and_1_out, and_2_out, and_3_out, and_4_out, not_1_out, not_2_out, not_3_out;

  not not_1 (not_1_out, yA1);
  not not_2 (not_2_out, yB1);
  not not_3 (not_3_out, c);
  and and_1 (and_1_out, not_1_out, not_2_out, c);
  and and_2 (and_2_out, yB1, not_3_out);
  and and_3 (and_3_out, yA1, not_3_out);
  and and_4 (and_4_out, yA1, yB1);
  or or_1 (O2, and_1_out, and_2_out, and_3_out, and_4_out);
endmodule

module intento100 (
  input  T,
  input  wA,
  input  xA,
  input  yA,
  input  zA,
  input  wB,
  input  xB,
  input  yB,
  input  zB,
  output O0,
  output O1,
  output O2,
  output O3
);

  wire and_1_out, and_2_out, and_3_out, and_4_out, and_5_out, and_6_out, and_7_out, and_8_out, and_9_out,
       and_10_out, and_11_out, and_12_out, and_13_out, and_14_out, and_15_out, and_16_out, and_17_out,
       and_18_out, and_19_out, and_20_out, and_21_out, and_22_out, and_23_out, and_24_out, and_25_out,
       and_26_out, and_27_out, and_28_out, and_29_out, and_30_out, and_31_out, and_32_out, not_1_out,
       not_2_out, not_3_out, not_4_out, not_5_out, not_6_out, not_7_out, not_8_out, not_9_out;

  not not_1 (not_1_out, T);
  not not_2 (not_2_out, wA);
  not not_3 (not_3_out, xA);
  not not_4 (not_4_out, yA);
  not not_5 (not_5_out, zA);
  not not_6 (not_6_out, wB);
  not not_7 (not_7_out, xB);
  not not_8 (not_8_out, yB);
  not not_9 (not_9_out, zB);
  and and_1 (and_1_out, not_1_out, wB);
  and and_2 (and_2_out, not_1_out, wA);
  and and_3 (and_3_out, T, not_3_out, not_4_out, zA);
  and and_4 (and_4_out, T, not_3_out, yA, not_5_out);
  and and_5 (and_5_out, T, xA, not_4_out, not_5_out);
  and and_6 (and_6_out, T, xA, yA, zA);
  and and_7 (and_7_out, not_1_out, xB);
  and and_8 (and_8_out, not_1_out, xA);
  and and_9 (and_9_out, not_2_out, xA, not_4_out, not_5_out);
  and and_10 (and_10_out, not_2_out, xA, yA, zA);
  and and_11 (and_11_out, wA, xA, not_4_out, zA);
  and and_12 (and_12_out, wA, xA, yA, not_5_out);
  and and_13 (and_13_out, T, not_2_out, not_3_out, not_4_out, zA);
  and and_14 (and_14_out, T, not_2_out, not_3_out, yA, not_5_out);
  and and_15 (and_15_out, T, wA, not_3_out, not_4_out, not_5_out);
  and and_16 (and_16_out, T, wA, not_3_out, yA, zA);
  and and_17 (and_17_out, not_1_out, wB);
  and and_18 (and_18_out, not_1_out, wA);
  and and_19 (and_19_out, T, not_7_out, not_8_out, zB);
  and and_20 (and_20_out, T, not_7_out, yB, not_9_out);
  and and_21 (and_21_out, T, xB, not_8_out, not_9_out);
  and and_22 (and_22_out, T, xB, yB, zB);
  and and_23 (and_23_out, not_1_out, zB);
  and and_24 (and_24_out, not_6_out, not_7_out, not_8_out, zB);
  and and_25 (and_25_out, not_6_out, xB, yB, zB);
  and and_26 (and_26_out, wB, not_7_out, yB, zB);
  and and_27 (and_27_out, wB, xB, not_8_out, zB);
  and and_28 (and_28_out, not_1_out, zA);
  and and_29 (and_29_out, T, not_6_out, not_7_out, yB, not_9_out);
  and and_30 (and_30_out, T, not_6_out, xB, not_8_out, not_9_out);
  and and_31 (and_31_out, T, wB, not_7_out, not_8_out, not_9_out);
  and and_32 (and_32_out, T, wB, xB, yB, not_9_out);
  or or_1 (O0, and_1_out, and_2_out, and_3_out, and_4_out, and_5_out, and_6_out);
  or or_2 (O2, and_17_out, and_18_out, and_19_out, and_20_out, and_21_out, and_22_out);
  or or_3 (O1, and_7_out, and_8_out, and_9_out, and_10_out, and_11_out, and_12_out, and_13_out, and_14_out, and_15_out, and_16_out);
  or or_4 (O3, and_23_out, and_24_out, and_25_out, and_26_out, and_27_out, and_28_out, and_29_out, and_30_out, and_31_out, and_32_out);
endmodule

module intento1000 (
  input  T,
  input  wA,
  input  xA,
  input  yA,
  input  zA,
  input  wB,
  input  xB,
  input  yB,
  input  zB,
  output O0,
  output O1,
  output O2,
  output O3
);

  wire and_1_out, and_2_out, and_3_out, and_4_out, and_5_out, and_6_out, and_7_out, and_8_out, and_9_out,
       and_10_out, and_11_out, and_12_out, and_13_out, and_14_out, and_15_out, and_16_out, and_17_out,
       and_18_out, and_19_out, and_20_out, and_21_out, and_22_out, and_23_out, and_24_out, and_25_out,
       and_26_out, and_27_out, and_28_out, and_29_out, and_30_out, and_31_out, and_32_out, not_1_out,
       not_2_out, not_3_out, not_4_out, not_5_out, not_6_out, not_7_out, not_8_out, not_9_out;

  not not_1 (not_1_out, T);
  not not_2 (not_2_out, wA);
  not not_3 (not_3_out, xA);
  not not_4 (not_4_out, yA);
  not not_5 (not_5_out, zA);
  not not_6 (not_6_out, wB);
  not not_7 (not_7_out, xB);
  not not_8 (not_8_out, yB);
  not not_9 (not_9_out, zB);
  and and_1 (and_1_out, not_1_out, wB);
  and and_2 (and_2_out, not_1_out, wA);
  and and_3 (and_3_out, T, not_3_out, not_4_out, zA);
  and and_4 (and_4_out, T, not_3_out, yA, not_5_out);
  and and_5 (and_5_out, T, xA, not_4_out, not_5_out);
  and and_6 (and_6_out, T, xA, yA, zA);
  and and_7 (and_7_out, not_1_out, xB);
  and and_8 (and_8_out, not_1_out, xA);
  and and_9 (and_9_out, not_2_out, xA, not_4_out, not_5_out);
  and and_10 (and_10_out, not_2_out, xA, yA, zA);
  and and_11 (and_11_out, wA, xA, not_4_out, zA);
  and and_12 (and_12_out, wA, xA, yA, not_5_out);
  and and_13 (and_13_out, T, not_2_out, not_3_out, not_4_out, zA);
  and and_14 (and_14_out, T, not_2_out, not_3_out, yA, not_5_out);
  and and_15 (and_15_out, T, wA, not_3_out, not_4_out, not_5_out);
  and and_16 (and_16_out, T, wA, not_3_out, yA, zA);
  and and_17 (and_17_out, not_1_out, wB);
  and and_18 (and_18_out, not_1_out, wA);
  and and_19 (and_19_out, T, not_7_out, not_8_out, zB);
  and and_20 (and_20_out, T, not_7_out, yB, not_9_out);
  and and_21 (and_21_out, T, xB, not_8_out, not_9_out);
  and and_22 (and_22_out, T, xB, yB, zB);
  and and_23 (and_23_out, not_1_out, zB);
  and and_24 (and_24_out, not_6_out, not_7_out, not_8_out, zB);
  and and_25 (and_25_out, not_6_out, xB, yB, zB);
  and and_26 (and_26_out, wB, not_7_out, yB, zB);
  and and_27 (and_27_out, wB, xB, not_8_out, zB);
  and and_28 (and_28_out, not_1_out, zA);
  and and_29 (and_29_out, T, not_6_out, not_7_out, yB, not_9_out);
  and and_30 (and_30_out, T, not_6_out, xB, not_8_out, not_9_out);
  and and_31 (and_31_out, T, wB, not_7_out, not_8_out, not_9_out);
  and and_32 (and_32_out, T, wB, xB, yB, not_9_out);
  or or_1 (O0, and_1_out, and_2_out, and_3_out, and_4_out, and_5_out, and_6_out);
  or or_2 (O2, and_17_out, and_18_out, and_19_out, and_20_out, and_21_out, and_22_out);
  or or_3 (O1, and_7_out, and_8_out, and_9_out, and_10_out, and_11_out, and_12_out, and_13_out, and_14_out, and_15_out, and_16_out);
  or or_4 (O3, and_23_out, and_24_out, and_25_out, and_26_out, and_27_out, and_28_out, and_29_out, and_30_out, and_31_out, and_32_out);
endmodule

module led (
  input  o0,
  input  o1,
  input  o2,
  input  o3,
  output a,
  output b,
  output c,
  output d,
  output e,
  output f,
  output g
);

  wire and_1_out, and_2_out, and_3_out, and_4_out, and_5_out, and_6_out, and_7_out, and_8_out, and_9_out,
       and_10_out, and_11_out, and_12_out, and_13_out, and_14_out, and_15_out, and_16_out, and_17_out,
       and_18_out, and_19_out, and_20_out, and_21_out, and_22_out, and_23_out, and_24_out, and_25_out,
       and_26_out, nor_1_out, nor_2_out, nor_3_out, nor_4_out, nor_5_out, nor_6_out, nor_7_out, nor_8_out;

  nor nor_1 (nor_1_out, o1, o3);
  and and_1 (and_1_out, ~o0, o2);  // AND_Gate
  and and_2 (and_2_out, ~o0, o1, o3);  // AND_Gate
  and and_3 (and_3_out, o1, o2);
  and and_4 (and_4_out, o0, ~o1, ~o2);  // AND_Gate
  and and_5 (and_5_out, o0, ~o3);  // AND_Gate
  nor nor_2 (nor_2_out, o0, o3);
  nor nor_3 (nor_3_out, o0, o2, o3);
  nor nor_4 (nor_4_out, o1, o3);
  and and_6 (and_6_out, ~o0, o2, o3);  // AND_Gate
  and and_7 (and_7_out, o0, ~o2, o3);  // AND_Gate
  nor nor_5 (nor_5_out, o0, o2);
  and and_8 (and_8_out, ~o0, o3);  // AND_Gate
  and and_9 (and_9_out, ~o2, o3);  // AND_Gate
  and and_10 (and_10_out, ~o0, o1);  // AND_Gate
  and and_11 (and_11_out, o0, ~o1);  // AND_Gate
  nor nor_6 (nor_6_out, o0, o1, o3);
  and and_12 (and_12_out, ~o1, o2, o3);  // AND_Gate
  and and_13 (and_13_out, o1, o2, ~o3);  // AND_Gate
  and and_14 (and_14_out, o0, ~o2);  // AND_Gate
  nor nor_7 (nor_7_out, o1, o3);
  and and_15 (and_15_out, o2, ~o3);  // AND_Gate
  and and_16 (and_16_out, o0, o2);
  and and_17 (and_17_out, o0, o1);
  nor nor_8 (nor_8_out, o2, o3);
  and and_18 (and_18_out, ~o0, o1, ~o2);  // AND_Gate
  and and_19 (and_19_out, o1, ~o3);  // AND_Gate
  and and_20 (and_20_out, o0, ~o1);  // AND_Gate
  and and_21 (and_21_out, o0, o2);
  and and_22 (and_22_out, ~o1, o2);  // AND_Gate
  and and_23 (and_23_out, o2, ~o3);  // AND_Gate
  and and_24 (and_24_out, ~o0, o1, ~o2);  // AND_Gate
  and and_25 (and_25_out, o0, ~o1);  // AND_Gate
  and and_26 (and_26_out, o0, o3);
  or or_1 (a, nor_1_out, and_1_out, and_2_out, and_3_out, and_4_out, and_5_out);
  or or_2 (b, nor_2_out, nor_3_out, nor_4_out, and_6_out, and_7_out);
  or or_3 (c, nor_5_out, and_8_out, and_9_out, and_10_out, and_11_out);
  or or_4 (d, nor_6_out, and_12_out, and_13_out, and_14_out);
  or or_5 (e, nor_7_out, and_15_out, and_16_out, and_17_out);
  or or_6 (f, nor_8_out, and_18_out, and_19_out, and_20_out, and_21_out);
  or or_7 (g, and_22_out, and_23_out, and_24_out, and_25_out, and_26_out);
endmodule

module l (
  input  o0,
  input  o1,
  input  o2,
  input  o3,
  output a,
  output b,
  output c,
  output d,
  output e,
  output f,
  output g
);

  wire and_1_out, and_2_out, and_3_out, and_4_out, and_5_out, and_6_out, and_7_out, and_8_out, and_9_out,
       and_10_out, and_11_out, and_12_out, and_13_out, and_14_out, and_15_out, and_16_out, and_17_out,
       and_18_out, and_19_out, and_20_out, and_21_out, and_22_out, and_23_out, and_24_out, and_25_out,
       and_26_out, and_27_out, and_28_out, and_29_out, and_30_out, and_31_out, and_32_out, and_33_out,
       and_34_out, not_1_out, not_2_out, not_3_out, not_4_out;

  not not_1 (not_1_out, o0);
  not not_2 (not_2_out, o1);
  not not_3 (not_3_out, o2);
  not not_4 (not_4_out, o3);
  and and_1 (and_1_out, not_2_out, not_4_out);
  and and_2 (and_2_out, not_1_out, o2);
  and and_3 (and_3_out, not_1_out, o1, o3);
  and and_4 (and_4_out, o1, o2);
  and and_5 (and_5_out, o0, not_2_out, not_3_out);
  and and_6 (and_6_out, o0, not_4_out);
  and and_7 (and_7_out, not_1_out, not_2_out);
  and and_8 (and_8_out, not_1_out, not_3_out, not_4_out);
  and and_9 (and_9_out, not_2_out, not_4_out);
  and and_10 (and_10_out, not_1_out, o2, o3);
  and and_11 (and_11_out, o0, not_3_out, o3);
  and and_12 (and_12_out, not_1_out, not_3_out);
  and and_13 (and_13_out, not_1_out, o3);
  and and_14 (and_14_out, not_3_out, o3);
  and and_15 (and_15_out, not_1_out, o1);
  and and_16 (and_16_out, o0, not_2_out);
  and and_17 (and_17_out, not_1_out, not_2_out, not_4_out);
  and and_18 (and_18_out, not_2_out, o2, o3);
  and and_19 (and_19_out, o1, o2, not_4_out);
  and and_20 (and_20_out, o0, not_3_out);
  and and_21 (and_21_out, not_2_out, not_4_out);
  and and_22 (and_22_out, o2, not_4_out);
  and and_23 (and_23_out, o0, o2);
  and and_24 (and_24_out, o0, o1);
  and and_25 (and_25_out, not_3_out, not_4_out);
  and and_26 (and_26_out, not_1_out, o1, not_3_out);
  and and_27 (and_27_out, o1, not_4_out);
  and and_28 (and_28_out, o0, not_2_out);
  and and_29 (and_29_out, o0, o2);
  and and_30 (and_30_out, not_2_out, o2);
  and and_31 (and_31_out, o2, not_4_out);
  and and_32 (and_32_out, not_1_out, o1, not_3_out);
  and and_33 (and_33_out, o0, not_2_out);
  and and_34 (and_34_out, o0, o3);
  or or_1 (a, and_1_out, and_2_out, and_3_out, and_4_out, and_5_out, and_6_out);
  or or_2 (b, and_7_out, and_8_out, and_9_out, and_10_out, and_11_out);
  or or_3 (c, and_12_out, and_13_out, and_14_out, and_15_out, and_16_out);
  or or_4 (d, and_17_out, and_18_out, and_19_out, and_20_out);
  or or_5 (e, and_21_out, and_22_out, and_23_out, and_24_out);
  or or_6 (f, and_25_out, and_26_out, and_27_out, and_28_out, and_29_out);
  or or_7 (g, and_30_out, and_31_out, and_32_out, and_33_out, and_34_out);
endmodule

module halfAdder (
  input  xB,
  input  yB,
  input  zB,
  output O2
);

  wire xor_1_out;

  xor xor_1 (xor_1_out, xB, yB);
  xor xor_2 (O2, xor_1_out, zB);
endmodule

module a (
  input  o0,
  input  o1,
  input  o2,
  input  o3
);

  wire and_1_out, and_2_out, and_3_out, and_4_out, and_5_out, and_6_out, and_7_out, and_8_out, and_9_out,
       and_10_out, and_11_out, and_12_out, and_13_out, and_14_out, and_15_out, and_16_out, and_17_out,
       and_18_out, and_19_out, not_1_out, not_2_out, not_3_out, not_4_out, or_1_out, xor_1_out;

  not not_1 (not_1_out, o0);
  not not_2 (not_2_out, o1);
  not not_3 (not_3_out, o2);
  not not_4 (not_4_out, o3);
  and and_1 (and_1_out, not_2_out, not_4_out);
  and and_2 (and_2_out, not_1_out, o2);
  and and_3 (and_3_out, not_1_out, o1, o3);
  and and_4 (and_4_out, o1, o2);
  and and_5 (and_5_out, o0, not_2_out, not_3_out);
  and and_6 (and_6_out, o0, not_4_out);
  or or_1 (or_1_out, not_4_out, not_1_out);
  and and_7 (and_7_out, or_1_out, not_3_out);
  and and_8 (and_8_out, o3, not_2_out, o0);
  and and_9 (and_9_out, not_3_out, not_1_out);
  and and_10 (and_10_out, not_1_out, o3);
  and and_11 (and_11_out, not_3_out, o3);
  xor xor_1 (xor_1_out, o0, o1);
  and and_12 (and_12_out, not_1_out, not_2_out, not_4_out);
  and and_13 (and_13_out, not_2_out, o2, o3);
  and and_14 (and_14_out, o1, o2, not_4_out);
  and and_15 (and_15_out, o0, not_3_out);
  and and_16 (and_16_out, not_2_out, not_4_out);
  and and_17 (and_17_out, o2, not_4_out);
  and and_18 (and_18_out, o0, o2);
  and and_19 (and_19_out, o1, o0);
  // OR_Gate or_2 has open pins: in0=and_1_out, in1=and_2_out, in2=and_3_out, in3=and_4_out, in4=and_5_out, in5=and_6_out, out=open
  // OR_Gate or_3 has open pins: in0=and_7_out, in1=and_8_out, in2=o3, out=open
  // OR_Gate or_4 has open pins: in0=and_9_out, in1=and_10_out, in2=and_11_out, in3=xor_1_out, out=open
  // OR_Gate or_5 has open pins: in0=and_12_out, in1=and_13_out, in2=and_14_out, in3=and_15_out, out=open
  // OR_Gate or_6 has open pins: in0=and_16_out, in1=and_17_out, in2=and_18_out, in3=and_19_out, out=open
endmodule

module gx (
  input  f,
  input  w,
  output O
);

  wire not_1_out;

  not not_1 (not_1_out, f);
  Multiplexer #(.enable("false")) multiplexer_1 (.in0(f), .in1(not_1_out), .out(O), .sel(w));
endmodule
