// Logisim project sumaAB.circ as structural Verilog: 4 circuits, main circuit main
module main (
  input  wA,
  input  wB,
  input  x_A,
  input  x_B,
  input  y_A,
  input  y_B,
  input  z_A,
  input  z_B,
  input  in_9,
  input  z_A2,
  input  z_B2,
  input  in_12,
  output o0,
  output o1,
  output o2,
  output o3,
  output o_32,
  output out_18
);

  wire and_1_out, and_2_out, and_3_out, and_4_out, not_1_out, not_2_out, or_1_out, or_2_out, Resto_out,
       xor_1_out, xor_2_out, xor_3_out;

  xor xor_1 (xor_1_out, y_A, y_B);
  and and_1 (and_1_out, y_B, y_A);
  and Resto (Resto_out, z_A, z_B);
  xor Suma (o3, z_A, z_B);
  not not_1 (not_1_out, in_9);
  not not_2 (not_2_out, in_12);
  and and_2 (and_2_out, xor_1_out, Resto_out);
  Multiplexer #(.enable("false"), .select(2)) multiplexer_1 (
    .in0(in_9), .in1(not_1_out), .in2(not_1_out), .in3(in_9), .out(o_32), .sel({z_B2, z_A2}));
  Multiplexer #(.enable("false"), .select(2)) multiplexer_2 (
    .in0(in_12), .in1(in_12), .in2(in_12), .in3(not_2_out), .out(out_18), .sel({z_B2, z_A2}));
  xor xor_2 (xor_2_out, wA, wB);
  and and_3 (and_3_out, x_A, x_B);
  xor xor_3 (xor_3_out, x_A, x_B);
  or or_1 (or_1_out, and_2_out, and_1_out);
  and and_4 (and_4_out, xor_3_out, or_1_out);
  xor xor_4 (o2, xor_1_out, Resto_out);
  or or_2 (or_2_out, and_4_out, and_3_out);
  xor xor_5 (o1, xor_3_out, or_1_out);
  xor xor_6 (o0, xor_2_out, or_2_out);

  // Notes on the sheet:
  //   Suma
  //   Resto
endmodule

module fulladder3input (
  input  wA,
  input  wB,
  input  x_A,
  input  x_B,
  input  y_A,
  input  y_B,
  input  z_A,
  input  z_B,
  output o0,
  output o1,
  output o2,
  output o3
);

  wire and_1_out, and_2_out, and_3_out, and_4_out, or_1_out, or_2_out, Resto_out, xor_1_out, xor_2_out,
       xor_3_out;

  xor xor_1 (xor_1_out, y_A, y_B);
  and and_1 (and_1_out, y_B, y_A);
  and Resto (Resto_out, z_A, z_B);
  xor Suma (o3, z_A, z_B);
  and and_2 (and_2_out, xor_1_out, Resto_out);
  xor xor_2 (xor_2_out, wA, wB);
  and and_3 (and_3_out, x_A, x_B);
  xor xor_3 (xor_3_out, x_A, x_B);
  or or_1 (or_1_out, and_2_out, and_1_out);
  and and_4 (and_4_out, xor_3_out, or_1_out);
  xor xor_4 (o2, xor_1_out, Resto_out);
  or or_2 (or_2_out, and_4_out, and_3_out);
  xor xor_5 (o1, xor_3_out, or_1_out);
  xor xor_6 (o0, xor_2_out, or_2_out);
endmodule

module fullAdder (
  input  cin,
  input  B,
  input  A,
  output Sum,
  output cout
);

  wire and_1_out, and_2_out, and_3_out, and_4_out, and_5_out, and_6_out, and_7_out, not_1_out, not_2_out,
       not_3_out;

  not not_1 (not_1_out, cin);
  not not_2 (not_2_out, B);
  not not_3 (not_3_out, A);
  and and_1 (and_1_out, not_1_out, not_2_out, A);
  and and_2 (and_2_out, not_1_out, B, not_3_out);
  and and_3 (and_3_out, cin, not_2_out, not_3_out);
  and and_4 (and_4_out, cin, B, A);
  and and_5 (and_5_out, B, A);
  and and_6 (and_6_out, cin, A);
  and and_7 (and_7_out, cin, B);
  or or_1 (Sum, and_1_out, and_2_out, and_3_out, and_4_out);
  or or_2 (cout, and_5_out, and_6_out, and_7_out);
endmodule

module soloFullAdder (
  input  A,
  input  B,
  input  Cin,
  output Cout,
  output Sum
);

  wire and_1_out, and_2_out, xor_1_out;

  xor xor_1 (xor_1_out, A, B);
  and and_1 (and_1_out, B, A);
  and and_2 (and_2_out, xor_1_out, Cin);
  or or_1 (Cout, and_2_out, and_1_out);
  xor xor_2 (Sum, xor_1_out, Cin);
endmodule
