// Logisim project Intento2T3.circ as structural Verilog: 7 circuits, main circuit main
module main (
  input  [7:0] X,
  input  CLK,
  input  [1:0] M,
  output [7:0] P,
  output [7:0] S
);

  wire [7:0] logicflipflop8bits_1_xout;

  logicFlipFlop8bits logicflipflop8bits_1 (.X(X), .CLK(CLK), .P(P), .Xout(logicflipflop8bits_1_xout));
  SLogic slogic_1 (.X(logicflipflop8bits_1_xout), .P(P), .M(M), .S(S));
  LED led_1 (.in(S[7]));
  LED led_2 (.in(S[6]));
  LED led_3 (.in(S[5]));
  LED led_4 (.in(S[4]));
  LED led_5 (.in(S[2]));
  LED led_6 (.in(S[3]));
  LED led_7 (.in(S[1]));
  LED led_8 (.in(S[0]));
endmodule

module SLogic (
  input  [7:0] X,
  input  [7:0] P,
  input  [1:0] M,
  output [7:0] S
);

  wire [7:0] and_1_out, or_1_out, resta_1_s, suma_1_s;

  assign or_1_out = X | P;  // OR_Gate or_1, 8 bits wide
  assign and_1_out = X & P;  // AND_Gate and_1, 8 bits wide
  Suma suma_1 (.X(X), .P(P), .S(suma_1_s));
  Resta resta_1 (.X(X), .P(P), .S(resta_1_s));
  Multiplexer #(.enable("false"), .select(2), .width(8)) multiplexer_1 (
    .in0(suma_1_s), .in1(resta_1_s), .in2(or_1_out), .in3(and_1_out), .out(S), .sel(M));
endmodule

module logicFlipFlop8bits (
  input  [7:0] X,
  input  CLK,
  output [7:0] P,
  output [7:0] Xout
);

  logicFlipFlop logicflipflop_1 (.X(X[0]), .CLK(CLK), .P(P[0]), .Xout(Xout[0]));
  logicFlipFlop logicflipflop_2 (.X(X[1]), .CLK(CLK), .P(P[1]), .Xout(Xout[1]));
  logicFlipFlop logicflipflop_3 (.X(X[2]), .CLK(CLK), .P(P[2]), .Xout(Xout[2]));
  logicFlipFlop logicflipflop_4 (.X(X[3]), .CLK(CLK), .P(P[3]), .Xout(Xout[3]));
  logicFlipFlop logicflipflop_5 (.X(X[4]), .CLK(CLK), .P(P[4]), .Xout(Xout[4]));
  logicFlipFlop logicflipflop_6 (.X(X[5]), .CLK(CLK), .P(P[5]), .Xout(Xout[5]));
  logicFlipFlop logicflipflop_7 (.X(X[6]), .CLK(CLK), .P(P[6]), .Xout(Xout[6]));
  logicFlipFlop logicflipflop_8 (.X(X[7]), .CLK(CLK), .P(P[7]), .Xout(Xout[7]));
endmodule

module logicFlipFlop (
  input  X,
  input  CLK,
  output P,
  output Xout
);

  wire nand_1_out, nand_2_out, nand_4_out, nand_5_out, nand_6_out, nand_8_out, not_1_out, not_2_out,
       not_3_out;

  not not_1 (not_1_out, X);
  not not_2 (not_2_out, CLK);
  nand nand_1 (nand_1_out, X, not_2_out);
  nand nand_2 (nand_2_out, not_1_out, not_2_out);
  nand nand_3 (Xout, nand_1_out, nand_4_out);
  nand nand_4 (nand_4_out, Xout, nand_2_out);
  not not_3 (not_3_out, Xout);
  nand nand_5 (nand_5_out, Xout, CLK);
  nand nand_6 (nand_6_out, not_3_out, CLK);
  nand nand_7 (P, nand_5_out, nand_8_out);
  nand nand_8 (nand_8_out, P, nand_6_out);

  // Notes on the sheet:
  //   FF1
  //   FF2
  //   X
  //   P(X)
endmodule

module Suma (
  input  [7:0] X,
  input  [7:0] P,
  output [7:0] S
);

  wire fulladder_1_cout, fulladder_2_cout, fulladder_3_cout, fulladder_4_cout, fulladder_5_cout,
       fulladder_6_cout, fulladder_7_cout;

  FullAdder fulladder_1 (.Cin(1'b0), .A(X[0]), .B(P[0]), .Cout(fulladder_1_cout), .Res(S[0]));
  FullAdder fulladder_2 (.Cin(fulladder_1_cout), .A(X[1]), .B(P[1]), .Cout(fulladder_2_cout), .Res(S[1]));
  FullAdder fulladder_3 (.Cin(fulladder_2_cout), .A(X[2]), .B(P[2]), .Cout(fulladder_3_cout), .Res(S[2]));
  FullAdder fulladder_4 (.Cin(fulladder_3_cout), .A(X[3]), .B(P[3]), .Cout(fulladder_4_cout), .Res(S[3]));
  FullAdder fulladder_5 (.Cin(fulladder_4_cout), .A(X[4]), .B(P[4]), .Cout(fulladder_5_cout), .Res(S[4]));
  FullAdder fulladder_6 (.Cin(fulladder_5_cout), .A(X[5]), .B(P[5]), .Cout(fulladder_6_cout), .Res(S[5]));
  FullAdder fulladder_7 (.Cin(fulladder_6_cout), .A(X[6]), .B(P[6]), .Cout(fulladder_7_cout), .Res(S[6]));
  FullAdder fulladder_8 (.Cin(fulladder_7_cout), .A(X[7]), .B(P[7]), .Res(S[7]));  // open: Cout
endmodule

module FullAdder (
  input  Cin,
  input  A,
  input  B,
  output Cout,
  output Res
);

  wire and_1_out, and_2_out, xor_1_out;

  and and_1 (and_1_out, B, A);
  xor xor_1 (xor_1_out, A, B);
  and and_2 (and_2_out, xor_1_out, Cin);
  or or_1 (Cout, and_2_out, and_1_out);
  xor xor_2 (Res, xor_1_out, Cin);
endmodule

module Resta (
  input  [7:0] X,
  input  [7:0] P,
  output [7:0] S
);

  wire [7:0] not_1_out, suma_1_s;

  assign not_1_out = ~P;  // NOT_Gate not_1, 8 bits wide
  Suma suma_1 (.X(X), .P(not_1_out), .S(suma_1_s));
  Suma suma_2 (.X(suma_1_s), .P(8'h1), .S(S));
endmodule
